# Fritzing sketch TableSoccer (saved by Fritzing 0.9.0b)
breadboards: 1

parts:
  Part1 = Arduino Uno (Rev3) - ICSP
  LCD1 = LCD screen
  R7 = Trimmer Potentiometer [maximum_resistance=10kΩ package=THT]
  R8 = Resistor [tolerance=±5% resistance=1k package=THT]
  R9 = Resistor [tolerance=±5% resistance=1k package=THT]
  R10 = Resistor [tolerance=±5% resistance=1k package=THT]
  Part2 = Arduino Prototyping Shield
  J3 = female pin header, 6 pins [form="♀ (female)"]
  J4 = female pin header, 8 pins [form="♀ (female)"]
  J5 = female pin header, 8 pins [form="♀ (female)"]
  J6 = female pin header, 10 pins [form="♀ (female)"]
  LCD2 = LCD screen
  S5 = Square Pushbutton
  S6 = Square Pushbutton
  S7 = Square Pushbutton

nets:
  N1: Part1.A0, J3.pin6
  N2: Part1.ICSP_MOSI, Part1.D11_PWM/MOSI, LCD1.DB6, Part2.D11, J6.pin4, LCD2.DB6
  VSS: LCD1.VSS, LCD1.R/W, LCD1.LED-, R7.leg1, Part2.GND, J4.pin2, J4.pin3, J6.pin7, LCD2.VSS, LCD2.R/W, LCD2.LED-
  VDD: LCD1.VDD, R7.leg2, Part2.+5V, J4.pin4, LCD2.VDD
  N3: LCD1.V0, R7.wiper, LCD2.V0
  N4: LCD1.RS, Part2.D7, J5.pin8, LCD2.RS
  N5: LCD1.E, Part2.D8, J6.pin1, LCD2.E
  N6: LCD1.DB4, Part2.D9, J6.pin2, LCD2.DB4
  N7: LCD1.DB5, Part2.D10, J6.pin3, LCD2.DB5
  N8: LCD1.DB7, Part2.D12, J6.pin5, LCD2.DB7
  N9: LCD1.LED+, Part2.D13, J6.pin6, LCD2.LED+
  N10: R8.Pin_0, S5.leg1
  N11: R8.Pin_1, R9.Pin_0, S6.leg1
  N12: R9.Pin_1, R10.Pin_0, S7.leg1
  N13: Part2.A0, S5.leg0, S6.leg0, S7.leg0
  N14: Part2.A1, J3.pin5
  N15: Part2.A2, J3.pin4
  N16: Part2.A3, J3.pin3
  N17: Part2.A4, J3.pin2
  N18: Part2.A5, J3.pin1
  N19: Part2.D0(RX), J5.pin1
  N20: Part2.D1(TX), J5.pin2
  N21: Part2.D2, J5.pin3
  N22: Part2.D3, J5.pin4
  N23: Part2.D4, J5.pin5
  N24: Part2.D5, J5.pin6
  N25: Part2.D6, J5.pin7
  N26: Part2.IOREF, J4.pin7, J4.pin8
  N27: Part2.RESET, J4.pin6
  N28: Part2.3.3V, J4.pin5
  N29: Part2.+9V, J4.pin1
  N30: Part2.AREF, J6.pin8
  N31: Part2.SDA, J6.pin9
  N32: Part2.SCL, J6.pin10

notes:
  Start
  Score
  blue
  Score
  red
